# Fritzing sketch Meteostation (saved by Fritzing 0.9.3b)
breadboards: 1

parts:
  Часть1 = Arduino Uno (Rev3)
  LCM2004_IIC1 = LCM1602 IIC [part_number="LCM2004 IIC" chip_label="LCM2004 IIC" package="DIP (Dual Inline) [THT]"]
  LCD1 = LCD screen
  DHT1 = DHT22 Humidity and Temperature Sensor
  R1 = Resistor [tolerance=±5% resistance=10k package="2512 [SMD]"]
  S1 = Pushbutton [package="[THT]"]
  S2 = Pushbutton [package="[THT]"]
  Часть2 = Real Time Clock Module - DS1307 RTC Breakout Board
  Часть3 = Barometric Pressure Sensor - BMP180 Breakout (GY-68)

nets:
  N1: Часть1.A4/SDA, LCM2004_IIC1.SDA, Часть2.SDA, Часть3.SDA
  N2: Часть1.A5/SCL, LCM2004_IIC1.SCL, Часть2.SCL, Часть3.SCL
  N3: Часть1.D2, DHT1.DATA, R1.Pin_0
  N4: Часть1.D3_PWM, S1.Pin_3, S1.Pin_4
  N5: Часть1.D4, S2.Pin_3, S2.Pin_4
  5V: Часть1.5V, LCM2004_IIC1.VCC, DHT1.VDD, R1.Pin_1, Часть2.5V, Часть3.VCC
  GND: Часть1.GND, LCM2004_IIC1.GND, DHT1.GND, S1.Pin_1, S1.Pin_2, S2.Pin_1, S2.Pin_2, Часть2.GND, Часть3.GND
  VSS: LCM2004_IIC1.VSS, LCD1.VSS
  VDD: LCM2004_IIC1.VDD, LCD1.VDD
  N6: LCM2004_IIC1.V0, LCD1.V0
  N7: LCM2004_IIC1.RS, LCD1.RS
  N8: LCM2004_IIC1.RW, LCD1.R/W
  N9: LCM2004_IIC1.E, LCD1.E
  N10: LCM2004_IIC1.D0, LCD1.DB0
  N11: LCM2004_IIC1.D1, LCD1.DB1
  N12: LCM2004_IIC1.D2, LCD1.DB2
  N13: LCM2004_IIC1.D3, LCD1.DB3
  N14: LCM2004_IIC1.D4, LCD1.DB4
  N15: LCM2004_IIC1.D5, LCD1.DB5
  N16: LCM2004_IIC1.D6, LCD1.DB6
  N17: LCM2004_IIC1.D7, LCD1.DB7
  N18: LCM2004_IIC1.A, LCD1.LED+
  N19: LCM2004_IIC1.K, LCD1.LED-
  N20: LCM2004_IIC1.LED_A, LCM2004_IIC1.LED_B

custom parts:
  LCM1602 IIC: I2C-Module to use a 1602 or 2004 LCD on with the wire.h libory Serial LCD Modul
